# Fritzing sketch LED_Group_Perfboard (saved by Fritzing 0.9.2b)
perfboards: 1

parts:
  C3 = Ceramic Capacitor [capacitance=0.1µF package="100 mil [THT, multilayer]"]
  R1 = Resistor [tolerance=±5% resistance=180 power=250mW package=THT]
  LED10 = LED - 5mm [color="Infrared (940nm)" current=20mA package="5 mm [THT]"]
  IR1 = TSOP312.., 314.. [package=THT]
  LED1 = LED - 5mm [color="Red (633nm)" part_number="AdaFruit ADA679" current=20mA package="5 mm [THT]"]
  Q1 = PNP-Transistor [part_number=2N2222 package="TO92 [THT]"]
  J1 = female pin header, 2 pins [form="♀ (female)"]
  J2 = female pin header, 2 pins [form="♀ (female)"]
  J3 = female pin header, 2 pins [form="♀ (female)"]
  J4 = female pin header, 2 pins [form="♀ (female)"]
  R2 = Resistor [tolerance=±5% resistance=180 power=250mW package=THT]
  LED2 = LED - 5mm [color="Red (633nm)" part_number="AdaFruit ADA679" current=20mA package="5 mm [THT]"]
  R3 = Resistor [tolerance=±5% resistance=180 power=250mW package=THT]
  LED3 = LED - 5mm [color="Red (633nm)" part_number="AdaFruit ADA679" current=20mA package="5 mm [THT]"]
  R4 = Resistor [tolerance=±5% resistance=180 power=250mW package=THT]
  LED4 = LED - 5mm [color="Red (633nm)" part_number="AdaFruit ADA679" current=20mA package="5 mm [THT]"]
  R5 = Resistor [tolerance=±5% resistance=180 power=250mW package=THT]
  LED5 = LED - 5mm [color="Red (633nm)" part_number="AdaFruit ADA679" current=20mA package="5 mm [THT]"]
  R6 = Resistor [tolerance=±5% resistance=180 power=250mW package=THT]
  LED6 = LED - 5mm [color="Red (633nm)" part_number="AdaFruit ADA679" current=20mA package="5 mm [THT]"]
  R7 = Resistor [tolerance=±5% resistance=180 power=250mW package=THT]
  LED7 = LED - 5mm [color="Red (633nm)" part_number="AdaFruit ADA679" current=20mA package="5 mm [THT]"]
  R8 = Resistor [tolerance=±5% resistance=180 power=250mW package=THT]
  LED8 = LED - 5mm [color="Red (633nm)" part_number="AdaFruit ADA679" current=20mA package="5 mm [THT]"]
  R9 = Resistor [tolerance=±5% resistance=180 power=250mW package=THT]
  LED9 = LED - 5mm [color="Red (633nm)" part_number="AdaFruit ADA679" current=20mA package="5 mm [THT]"]
  R10 = Resistor [tolerance=±5% resistance=1k package=THT]
  J6 = female pin header, 2 pins [form="♀ (female)"]
  J5 = male pin header, 2 pins [form="♂ (male)"]
  R11 = Resistor [tolerance=±5% resistance=180 package=THT]

nets:
  GND2: C3.0, IR1.GND, J4.pin2
  5.2V: C3.1, LED10.anode, J3.pin1, R11.Pin_0
  N1: R1.Pin_0, R2.Pin_0, R3.Pin_0, R4.Pin_0, R5.Pin_0, R6.Pin_0, R7.Pin_0, R8.Pin_0, R9.Pin_0, J6.pin1
  N2: R1.Pin_1, LED1.anode
  N3: LED10.cathode, J3.pin2
  N4: IR1.Vs, R11.Pin_1
  N5: IR1.Data, J4.pin1
  N6: LED1.cathode, LED2.cathode, LED3.cathode, LED4.cathode, LED5.cathode, LED6.cathode, LED7.cathode, LED8.cathode, LED9.cathode, J6.pin2
  N7: Q1.E, J5.pin2
  N8: Q1.B, R10.Pin_1
  GND: Q1.C, J1.pin2, J2.pin2
  5.1V: J1.pin1, J5.pin1
  N9: J2.pin1, R10.Pin_0
  N10: R2.Pin_1, LED2.anode
  N11: R3.Pin_1, LED3.anode
  N12: R4.Pin_1, LED4.anode
  N13: R5.Pin_1, LED5.anode
  N14: R6.Pin_1, LED6.anode
  N15: R7.Pin_1, LED7.anode
  N16: R8.Pin_1, LED8.anode
  N17: R9.Pin_1, LED9.anode
